# Fritzing sketch Bloque practico2 esquema (saved by Fritzing 0.9.1b)
breadboards: 2

parts:
  Parte1 = Arduino Uno (Rev3)
  7_Segment1 = 7 Segment Display
  7_Segment2 = 7 Segment Display
  7_Segment3 = 7 Segment Display
  7_Segment4 = 7 Segment Display
  R1 = Resistor [tolerance=±5% resistance=150 package=THT]
  R2 = Resistor [tolerance=±5% resistance=150 package=THT]
  R3 = Resistor [tolerance=±5% resistance=150 package=THT]
  R4 = Resistor [tolerance=±5% resistance=150 package=THT]

nets:
  N1: Parte1.A0, R4.Pin_1
  N2: Parte1.A1, R3.Pin_1
  N3: Parte1.A2, R2.Pin_1
  N4: Parte1.A3, R1.Pin_1
  N5: Parte1.D8, 7_Segment1.Segment_G, 7_Segment2.Segment_G, 7_Segment3.Segment_G, 7_Segment4.Segment_G
  N6: Parte1.D9_PWM, 7_Segment1.Segment_DP, 7_Segment2.Segment_DP, 7_Segment3.Segment_DP, 7_Segment4.Segment_DP
  N7: Parte1.D2, 7_Segment1.Segment_A, 7_Segment2.Segment_A, 7_Segment3.Segment_A, 7_Segment4.Segment_A
  N8: Parte1.D3_PWM, 7_Segment1.Segment_B, 7_Segment2.Segment_B, 7_Segment3.Segment_B, 7_Segment4.Segment_B
  N9: Parte1.D4, 7_Segment1.Segment_C, 7_Segment2.Segment_C, 7_Segment3.Segment_C, 7_Segment4.Segment_C
  N10: Parte1.D5_PWM, 7_Segment1.Segment_D, 7_Segment2.Segment_D, 7_Segment3.Segment_D, 7_Segment4.Segment_D
  N11: Parte1.D6_PWM, 7_Segment1.Segment_E, 7_Segment2.Segment_E, 7_Segment3.common_anode, 7_Segment4.Segment_E, R3.Pin_0
  N12: Parte1.D7, 7_Segment1.Segment_F, 7_Segment2.Segment_F, 7_Segment3.Segment_F, 7_Segment4.Segment_F
  N13: 7_Segment1.common_anode, R1.Pin_0
  N14: 7_Segment2.common_anode, R2.Pin_0
  N15: 7_Segment4.common_anode, R4.Pin_0
